// Logisim project 8r3_mux_with_2_4r2muxs.circ as structural Verilog: 1 circuit, main circuit main
module main (
  input  D0,
  input  D1,
  input  D2,
  input  D3,
  input  D4,
  input  D5,
  input  D6,
  input  D7,
  input  S2,
  input  [1:0] S1_S0,
  output out_11
);

  wire multiplexer_1_out, multiplexer_2_out;

  Multiplexer #(.select(2)) multiplexer_1 (
    .in0(D0), .in1(D1), .in2(D2), .in3(D3), .out(multiplexer_1_out), .sel(S1_S0));  // open: en
  Multiplexer #(.select(2)) multiplexer_2 (
    .in0(D4), .in1(D5), .in2(D6), .in3(D7), .out(multiplexer_2_out), .sel(S1_S0));  // open: en
  Multiplexer multiplexer_3 (.in0(multiplexer_1_out), .in1(multiplexer_2_out), .out(out_11), .sel(S2));  // open: en
endmodule
