// Logisim project assn_1.circ as structural Verilog: 2 circuits, main circuit main
module ALU_1_bit (
  input  Cin,
  input  A,
  input  B,
  input  Add_0_And_1,
  input  Enable,
  output Output,
  output Cout
);

  wire adder_1_out, and_1_out;

  Adder #(.width(1)) adder_1 (.a(A), .b(B), .out(adder_1_out), .cin(Cin), .cout(Cout));
  and and_1 (and_1_out, A, B);
  Multiplexer multiplexer_1 (.in0(adder_1_out), .in1(and_1_out), .out(Output), .sel(Add_0_And_1), .en(Enable));
endmodule

module main (
  input  Carry_in,
  input  [3:0] A,
  input  [3:0] B,
  input  Operation,
  input  Enable,
  output [3:0] Output,
  output Carry_out
);

  wire alu_1_bit_1_cout, alu_1_bit_2_cout, alu_1_bit_3_cout;

  ALU_1_bit alu_1_bit_1 (
    .Cin(Carry_in), .A(A[0]), .Output(Output[0]), .B(B[0]), .Add_0_And_1(Operation), .Cout(alu_1_bit_1_cout),
    .Enable(Enable));
  ALU_1_bit alu_1_bit_2 (
    .Cin(alu_1_bit_1_cout), .A(A[1]), .Output(Output[1]), .B(B[1]), .Add_0_And_1(Operation),
    .Cout(alu_1_bit_2_cout), .Enable(Enable));
  ALU_1_bit alu_1_bit_3 (
    .Cin(alu_1_bit_2_cout), .A(A[2]), .Output(Output[2]), .B(B[2]), .Add_0_And_1(Operation),
    .Cout(alu_1_bit_3_cout), .Enable(Enable));
  ALU_1_bit alu_1_bit_4 (
    .Cin(alu_1_bit_3_cout), .A(A[3]), .Output(Output[3]), .B(B[3]), .Add_0_And_1(Operation),
    .Cout(Carry_out), .Enable(Enable));
endmodule
