// Logisim project assn_2.circ as structural Verilog: 2 circuits, main circuit main
module main (
  input  in_1,
  input  [7:0] in_2,
  input  [7:0] in_3,
  input  [7:0] in_4,
  input  [2:0] in_5,
  output out_6
);

  wire n1_bit_alu_1_cout_0__bout_1, n1_bit_alu_2_cout_0__bout_1, n1_bit_alu_3_cout_0__bout_1,
       n1_bit_alu_4_cout_0__bout_1, n1_bit_alu_5_cout_0__bout_1, n1_bit_alu_6_cout_0__bout_1,
       n1_bit_alu_7_cout_0__bout_1;

  _1_Bit_ALU u_1_bit_alu_1 (
    .Cin_0__Bin_1(in_1), .A(in_2[0]), .B(in_3[0]), .Cout_0__Bout_1(n1_bit_alu_1_cout_0__bout_1),
    .Output(in_4[0]), .S2(in_5[2]), .S1(in_5[1]), .S0(in_5[0]));
  _1_Bit_ALU u_1_bit_alu_2 (
    .Cin_0__Bin_1(n1_bit_alu_1_cout_0__bout_1), .A(in_2[1]), .B(in_3[1]),
    .Cout_0__Bout_1(n1_bit_alu_2_cout_0__bout_1), .Output(in_4[1]), .S2(in_5[2]), .S1(in_5[1]), .S0(in_5[0]));
  _1_Bit_ALU u_1_bit_alu_3 (
    .Cin_0__Bin_1(n1_bit_alu_2_cout_0__bout_1), .A(in_2[2]), .B(in_3[2]),
    .Cout_0__Bout_1(n1_bit_alu_3_cout_0__bout_1), .Output(in_4[2]), .S2(in_5[2]), .S1(in_5[1]), .S0(in_5[0]));
  _1_Bit_ALU u_1_bit_alu_4 (
    .Cin_0__Bin_1(n1_bit_alu_3_cout_0__bout_1), .A(in_2[3]), .B(in_3[3]),
    .Cout_0__Bout_1(n1_bit_alu_4_cout_0__bout_1), .Output(in_4[3]), .S2(in_5[2]), .S1(in_5[1]), .S0(in_5[0]));
  _1_Bit_ALU u_1_bit_alu_5 (
    .Cin_0__Bin_1(n1_bit_alu_4_cout_0__bout_1), .A(in_2[4]), .B(in_3[4]),
    .Cout_0__Bout_1(n1_bit_alu_5_cout_0__bout_1), .Output(in_4[4]), .S2(in_5[2]), .S1(in_5[1]), .S0(in_5[0]));
  _1_Bit_ALU u_1_bit_alu_6 (
    .Cin_0__Bin_1(n1_bit_alu_5_cout_0__bout_1), .A(in_2[5]), .B(in_3[5]),
    .Cout_0__Bout_1(n1_bit_alu_6_cout_0__bout_1), .Output(in_4[5]), .S2(in_5[2]), .S1(in_5[1]), .S0(in_5[0]));
  _1_Bit_ALU u_1_bit_alu_7 (
    .Cin_0__Bin_1(n1_bit_alu_6_cout_0__bout_1), .A(in_2[6]), .B(in_3[6]),
    .Cout_0__Bout_1(n1_bit_alu_7_cout_0__bout_1), .Output(in_4[6]), .S2(in_5[2]), .S1(in_5[1]), .S0(in_5[0]));
  _1_Bit_ALU u_1_bit_alu_8 (
    .Cin_0__Bin_1(n1_bit_alu_7_cout_0__bout_1), .A(in_2[7]), .B(in_3[7]), .Cout_0__Bout_1(out_6),
    .Output(in_4[7]), .S2(in_5[2]), .S1(in_5[1]), .S0(in_5[0]));
endmodule

module _1_Bit_ALU (
  input  Cin_0__Bin_1,
  input  A,
  input  B,
  input  S2,
  input  S1,
  input  S0,
  output Cout_0__Bout_1,
  output Output
);

  wire adder_1_out, and_1_out, nor_1_out, or_1_out, xor_1_out, xor_2_out, xor_3_out;

  xor xor_1 (xor_1_out, A, S0);
  Adder #(.width(1)) adder_1 (.a(B), .b(xor_1_out), .out(adder_1_out), .cin(Cin_0__Bin_1), .cout(Cout_0__Bout_1));
  and and_1 (and_1_out, A, B);
  or or_1 (or_1_out, A, B);
  nor nor_1 (nor_1_out, A, B);
  xor xor_2 (xor_2_out, A, B);
  xor xor_3 (xor_3_out, adder_1_out, S0);
  Multiplexer #(.select(3), .enable("false")) multiplexer_1 (
    .in0(xor_3_out), .in1(xor_3_out), .in2(and_1_out), .in3(or_1_out), .in4(nor_1_out), .in5(xor_2_out),
    .out(Output), .sel({S2, S1, S0}));  // open: in6, in7
endmodule
